# Fritzing sketch Fritzing Wire Diagram + Schematic (saved by Fritzing 0.9.10b)
breadboards: 1

parts:
  U1 = ESP32S-HiLetgo [part_number=ESP32S-HiLetgo]
  LED1 = LED - 5mm [color="Red (633nm)" current=0.030 package="5 mm [THT]"]
  LED2 = LED - 5mm [color="Red (633nm)" current=0.030 package="5 mm [THT]"]
  R1 = Resistor [tolerance=±5% power=0.25 resistance=220 package=THT]
  R2 = Resistor [tolerance=±5% power=0.25 resistance=220 package=THT]
  J1 = Piezo Speaker
  R3 = Resistor [tolerance=±5% power=0.25 resistance=220 package=THT]
  Grove1 = Grove OLED 128x96
  RHT1 = Humidity and Temperature Sensor RHT03
  S1 = Pushbutton [package="[SMD]"]
  S2 = Pushbutton [package="[THT]"]
  S3 = Pushbutton [package="[THT]"]
  S4 = Pushbutton [package="[THT]"]
  R4 = Resistor [tolerance=±5% power=0.25 resistance=220 package=THT]
  R5 = Resistor [tolerance=±5% power=0.25 resistance=220 package=THT]
  R6 = Resistor [tolerance=±5% power=0.25 resistance=220 package=THT]
  R7 = Resistor [tolerance=±5% power=0.25 resistance=220 package=THT]

nets:
  VCC: U1.3.3, Grove1.VCC, RHT1.Vcc, R4.Pin_0, R5.Pin_0, R6.Pin_0, R7.Pin_0
  GND: U1.GND, R1.Pin_0, R2.Pin_0, R3.Pin_0, Grove1.GND, RHT1.GND_2, S1.Pin_1, S1.Pin_2, S2.Pin_1, S2.Pin_2, S3.Pin_1, S3.Pin_2, S4.Pin_1, S4.Pin_2
  N1: U1.GPIO11, J1.pin2
  N2: U1.GPIO6, S1.Pin_3, S1.Pin_4, R4.Pin_1
  N3: U1.GPIO7, S2.Pin_3, S2.Pin_4, R5.Pin_1
  N4: U1.GPIO8, S3.Pin_3, S3.Pin_4, R7.Pin_1
  N5: U1.GPIO15, S4.Pin_3, S4.Pin_4, R6.Pin_1
  N6: U1.GPIO2, LED1.anode
  N7: U1.GPIO0, LED2.anode
  N8: U1.GPIO4, RHT1.Data-signal
  N9: U1.GPIO21, Grove1.SDA
  N10: U1.GPIO22, Grove1.SCL
  N11: LED1.cathode, R1.Pin_1
  N12: LED2.cathode, R2.Pin_1
  N13: J1.pin1, R3.Pin_1

custom parts:
  ESP32S-HiLetgo: HiLetgo ESP-WROOM-32 ESP32 ESP-32S Development Board 2.4GHz Dual-Mode WiFi + Bluetooth Dual Cores Microcontroller The ESP32 integrated with Antenna switches, RF Balun, power amplifiers, low-noise amplifiers, filters, and management modules, and the entire solution occupies the least area of PCB. 2.4 GHz Wi-Fi plus Bluetooth dual-mode chip, with TSMC Ultra-low power consumption 40nm technology,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
